# Fritzing sketch esp32-38-pin-bme680-spi (saved by Fritzing 0.9.4)
breadboards: 1

parts:
  MH-ET_LIVE_ESP32_DEVKIT1 = MH-ET LIVE ESP32 DEVKIT 38 pins
  Part1 = Adafruit BME680 [part_number="Adafruit #3660"]

nets:
  3V3: MH-ET_LIVE_ESP32_DEVKIT1.3V3, Part1.VCC
  GND: MH-ET_LIVE_ESP32_DEVKIT1.GND, Part1.GND
  N1: MH-ET_LIVE_ESP32_DEVKIT1.IO23, Part1.SDI/SDA
  N2: MH-ET_LIVE_ESP32_DEVKIT1.IO19, Part1.SDO/ADR
  N3: MH-ET_LIVE_ESP32_DEVKIT1.IO18, Part1.SCK/SCL
  N4: MH-ET_LIVE_ESP32_DEVKIT1.IO5, Part1.CS

custom parts:
  MH-ET LIVE ESP32 DEVKIT 38 pins: http://mh.nodebb.com/topic/2/mh-et-live-esp32-devkit
