# Fritzing sketch rp2040-bme680-spi (saved by Fritzing 0.9.4)
breadboards: 1

parts:
  Mod1 = Raspberry Pi Pico
  Part1 = Adafruit BME680 [part_number="Adafruit #3660"]

nets:
  N1: Mod1.pin_21, Part1.SDO/ADR
  N2: Mod1.pin_22, Part1.CS
  N3: Mod1.pin_24, Part1.SCK/SCL
  N4: Mod1.pin_25, Part1.SDI/SDA
  N5: Mod1.pin_33, Mod1.pin_38, Part1.GND
  N6: Mod1.pin_36, Part1.3.3V

custom parts:
  Raspberry Pi Pico: Raspberry Pi Pico. Based around the RP2040 microcontroller the Pico is a low cost microcontroller device bringing Raspberry Pi quality, cost, and easy of use to the microcontroller space. Jan 2021, Split part in to two versions: tht (this one) and SMD. This one will drill holes for a .1 in header in pcb to allow plugging in the module as well as providing pads to solder the module to the top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
